# Fritzing sketch Schematic (saved by Fritzing 0.9.2b)
breadboards: 1

parts:
  Part1 = Arduino Uno (Rev3)
  R1 = Resistor [tolerance=±5% resistance=330 package=THT]
  R3 = Photocell (LDR) [package=THT]
  IC1 = L293D [package=THT]
  LED1 = LED - 3mm [color="White (6500K)" package="3 mm [THT]"]
  Part2 = Lithium Ion Polymer Battery 3.7v 1200mAh [part_number=258]
  Part3 = Lithium Ion Polymer Battery 3.7v 1200mAh [part_number=258]
  R5 = Resistor [tolerance=±5% resistance=220 package=THT]
  M1 = DC Motor
  M2 = DC Motor
  R4 = Resistor [tolerance=±5% resistance=10k package=THT]
  Part4 = HC-SR04
  SP1 = SPEAKER [package=pcb_mount_speaker]

nets:
  N1: Part1.A0, R3.pin_0, R4.Pin_1
  N2: Part1.D8, IC1.Enable_2
  N3: Part1.D9_PWM, IC1.In_3
  N4: Part1.D10_PWM/SS, IC1.In_4
  N5: Part1.D13/SCK, SP1.-
  GND: Part1.GND, R3.pin_1, IC1.0V, LED1.cathode, Part2.negative, Part3.negative, R4.Pin_0, Part4.GND, SP1.+
  N6: Part1.D3_PWM, Part4.Trig
  N7: Part1.D4, Part4.Echo
  N8: Part1.D5_PWM, IC1.Enable_1
  N9: Part1.D6_PWM, IC1.In_1
  N10: Part1.D7, IC1.In_2
  5V: Part1.5V, R1.Pin_0, IC1.+V, Part4.VCC
  N11: R1.Pin_1, LED1.anode
  N12: IC1.Out_1_(_Controlled_by_Enable_1_), M2.pin_2
  N13: IC1.Out_2_(_Controlled_by_Enable_1_), M2.pin_1
  N14: IC1.+Vmotor, R5.Pin_0
  N15: IC1.Out_3_(_Controlled_by_Enable_2_), M1.pin_1
  N16: IC1.Out_4_(_Controlled_by_Enable_2_), M1.pin_2
  N17: Part2.positive, Part3.positive, R5.Pin_1

custom parts:
  Lithium Ion Polymer Battery 3.7v 1200mAh: Lithium ion polymer (also known as 'lipo' or 'lipoly') batteries are thin, light and powerful. The output ranges from 4.2V when completely charged to 3.7V. This battery has a capacity of 1200mAh for a total of about 4.5 Wh. The batteries come pre-attached with a genuine 2-pin JST-PH connector as shown and include the necessary protection circuitry.
  HC-SR04: Ultrasonic sensor.

// code stored in the sketch: Sumobot.ino
#include "Music.h"

// Define sensor pin numbers.
#define TRIGGER 3 // The trigger pin for the ultrasonic sensor.
#define ECHO 4 // The echo pin for the ultrasonic sensor.
#define LDR_PIN A0 // The analog pin for LDR input,

// Define motor pin numbers.
#define LEFT_ENABLE 5 // The pin to turn the left motor on and off.
#define LEFT_FORWARD 6 // The pin to move the left motor forwards.
#define LEFT_BACKWARD 7 // The pin to move the left motor forwards.
#define RIGHT_ENABLE 8 // The pin to turn the left motor on and off.
#define RIGHT_FORWARD 9 // The pin to move the left motor forwards.
#define RIGHT_BACKWARD 10 // The pin to move the left motor forwards.

// Define constants.
#define SPEED_OF_SOUND 0.03434 // Speed of sound as STP in cm per microsecond.

// Variables for distance tracking.

// The ultrasonic sensor reading.
double frontDistance, backDistance;

// Define thresholds.
#define DISTANCE_THRESHOLD 100

// Information for playing notes.
unsigned int currentNote = 0; // The index of current note being played in the arrays.
unsigned long noteEndTime = 0; // The time in milliseconds to stop the current note.

#define SPEAKER_PIN 13 // Pin for the speaker.

// Setup the program.
void setup() {
	// Setup the ultrasonic sensor.
	pinMode(TRIGGER, OUTPUT); // Set the trigger pin as an output.
	pinMode(ECHO, INPUT); // Set the echo pin as an input.

	// Setup the motors.
	pinMode(LEFT_ENABLE, OUTPUT);
	pinMode(LEFT_FORWARD, OUTPUT);
	pinMode(LEFT_BACKWARD, OUTPUT);
	pinMode(RIGHT_ENABLE, OUTPUT);
	pinMode(RIGHT_FORWARD, OUTPUT);
	pinMode(RIGHT_BACKWARD, OUTPUT);

	Serial.begin(9600); // Start the serial communication.
}

// Read the LDR sensor.
void readLDR() {
	int lightLevel = analogRead(LDR_PIN);
	Serial.print("LDR: ");
	Serial.println(lightLevel);
}

// Read the ultrasonic sensors.
void readUltrasonic() {
	// Clear the trigger pin.
	digitalWrite(TRIGGER, LOW);
	delayMicroseconds(2);

	// Set the trigger pin on HIGH state for 10 micro seconds.
	digitalWrite(TRIGGER, HIGH);
	delayMicroseconds(10);
	digitalWrite(TRIGGER, LOW);

	// Read the echo pin.
	long duration = pulseIn(ECHO, HIGH); // Sound wave travel time in microseconds.

	frontDistance = duration * SPEED_OF_SOUND / 2.0;

	// Print the distance to the serial monitor.
	Serial.print("Front distance: ");
	Serial.println(frontDistance);
}

void forward() {
	Serial.println("Forward");

	// Enable motors.
	digitalWrite(LEFT_ENABLE, HIGH);
	digitalWrite(RIGHT_ENABLE, HIGH);

	// Move forward.
	digitalWrite(LEFT_FORWARD, HIGH);
	digitalWrite(LEFT_BACKWARD, LOW);
	digitalWrite(RIGHT_FORWARD, HIGH);
	digitalWrite(RIGHT_BACKWARD, LOW);
}

void left() {
	Serial.println("Left");

	// Enable motors.
	digitalWrite(LEFT_ENABLE, HIGH);
	digitalWrite(RIGHT_ENABLE, HIGH);

	// Move left.
	digitalWrite(LEFT_FORWARD, LOW);
	digitalWrite(LEFT_BACKWARD, HIGH);
	digitalWrite(RIGHT_FORWARD, HIGH);
	digitalWrite(RIGHT_BACKWARD, LOW);
}

void right() {
	Serial.println("Right");

	// Enable motors.
	digitalWrite(LEFT_ENABLE, HIGH);
	digitalWrite(RIGHT_ENABLE, HIGH);

	// Move right.
	digitalWrite(LEFT_FORWARD, HIGH);
	digitalWrite(LEFT_BACKWARD, LOW);
	digitalWrite(RIGHT_FORWARD, LOW);
	digitalWrite(RIGHT_BACKWARD, HIGH);
}

void backward() {
	Serial.println("Backward");

	// Enable motors.
	digitalWrite(LEFT_ENABLE, HIGH);
	digitalWrite(RIGHT_ENABLE, HIGH);

	// Move forward.
	digitalWrite(LEFT_FORWARD, LOW);
	digitalWrite(LEFT_BACKWARD, HIGH);
	digitalWrite(RIGHT_FORWARD, LOW);
	digitalWrite(RIGHT_BACKWARD, HIGH);
}

void stop() {
	Serial.println("Stop");

	digitalWrite(LEFT_ENABLE, LOW);
	digitalWrite(RIGHT_ENABLE, LOW);
}

void dance() {
	backward();
	left();
	right();
	backward();
}

// Play the next note in the song.
void updateMusic() {
	noTone(SPEAKER_PIN); // Ensure no tone is playing.

	if (currentNote >= (sizeof(melody) / sizeof(int))) { // If we have reached the end of the song.
		currentNote = 0;
	}

	int noteDuration = (1600 / noteDurations[currentNote]) * min(frontDistance,backDistance);
	if (melody[currentNote] == NOTE_REST) { // If this note is a rest, don't play anything.
		noteEndTime = millis() + noteDuration * 1.30; // Set the time for when to play the next note to noteDuration + 30%.
	} else {
		tone(SPEAKER_PIN, melody[currentNote], noteDuration);
		noteEndTime = millis() + noteDuration * 1.30; // Set the time for when to play the next note to noteDuration + 30%.
	}
	currentNote++;
}

void loop() {
	readLDR();
	readUltrasonic();

	if (frontDistance <= DISTANCE_THRESHOLD || backDistance <= DISTANCE_THRESHOLD) {
		if (frontDistance <= backDistance) {
			forward();
		} else if (backDistance < frontDistance) {
			backward();
		}
	} else {
		left();
	}

	//dance();
	if (millis() >= noteEndTime) {
		updateMusic();
	}
}
